# Fritzing sketch voltage_div_plus_pull_ups (saved by Fritzing 0.8.5b)
circuit board: 1.88986cm x 3.02764cm
breadboards: 1

parts:
  120 = Resistor [tolerance=±5% resistance=150 package=THT]
  330 = Resistor [tolerance=±5% resistance=330 package=THT]
  47 = Resistor [tolerance=±5% resistance=47 package=THT]
  10_k = Resistor [tolerance=±5% resistance=10k package=THT]
  10_k_2 = Resistor [tolerance=±5% resistance=10k package=THT]
  Wattuino = female pin header, 4 pins [form="♀ (female)"]
  Lens = female pin header, 4 pins [form="♀ (female)"]

nets:
  N1: 120.Pin_0, 10_k.Pin_0, 10_k_2.Pin_0, Wattuino.pin2
  N2: 120.Pin_1, 330.Pin_0, Lens.pin2
  N3: 330.Pin_1, 47.Pin_1
  N4: 47.Pin_0, Wattuino.pin1, Lens.pin1
  N5: 10_k.Pin_1, Wattuino.pin4, Lens.pin4
  N6: 10_k_2.Pin_1, Wattuino.pin3, Lens.pin3

notes:
  SDA SCL VCC GND
